# Fritzing sketch ATmelProgrammer (saved by Fritzing 0.9.0b)
circuit board: 6.17452cm x 4.68661cm
breadboards: 1

parts:
  ZIF_SOCKET = Aries 28-6574-10 28W ZIF Socket [part_number=28-6574-10]
  XTAL1 = Crystal [frequency="16 Mhz" package=THT]
  C1 = Ceramic Capacitor [capacitance=22pF package="100 mil [THT, multilayer]"]
  C2 = Ceramic Capacitor [capacitance=22pF package="100 mil [THT, multilayer]"]
  Arduino_Nano = Arduino Nano (Rev3.0)
  J1 = female pin header, 2 pins [form="♀ (female)"]
  J2 = female pin header, 2 pins [form="♀ (female)"]
  C3 = Electrolytic Capacitor [capacitance=10µF package="100 mil [THT, electrolytic]"]

nets:
  N1: ZIF_SOCKET.Pin_1, Arduino_Nano.D10
  N2: ZIF_SOCKET.Pin_4, J2.pin1
  N3: ZIF_SOCKET.Pin_7, Arduino_Nano.5V, J1.pin1
  N4: ZIF_SOCKET.Pin_8, C1.1, C2.0, Arduino_Nano.GND, J2.pin2, C3.-
  N5: ZIF_SOCKET.Pin_9, XTAL1.pin_0, C1.0
  N6: ZIF_SOCKET.Pin_10, XTAL1.pin_1, C2.1
  N7: ZIF_SOCKET.Pin_17, ZIF_SOCKET.Pin_25, Arduino_Nano.D11/MOSI
  N8: ZIF_SOCKET.Pin_18, ZIF_SOCKET.Pin_24, ZIF_SOCKET.Pin_26, Arduino_Nano.D12/MISO
  N9: ZIF_SOCKET.Pin_19, ZIF_SOCKET.Pin_27, Arduino_Nano.D13/SCK
  N10: ZIF_SOCKET.Pin_28, J1.pin2
  N11: Arduino_Nano.RESET, C3.+

notes:
  ATMega328 : J1=Off J2=Off
  ATTiny85 : J1=On J2=On
