# Fritzing sketch SmartCarController (saved by Fritzing 0.9.3b)
circuit board: 7.26679cm x 4.65651cm

parts:
  ATMega328PU = atmega328 [package=dip]
  ATTiny85 = attiny85 [package=dip]
  R1 = Resistor [tolerance=±5% resistance=10k package=THT]
  XTAL1 = Crystal [frequency="16 Mhz" package=THT]
  C1 = Ceramic Capacitor [capacitance=22pF package="200 mil [THT, multilayer]"]
  C2 = Ceramic Capacitor [capacitance=22pF package="200 mil [THT, multilayer]"]
  ULN_2003 = ULN2003A [package="DIP16 [THT]"]
  J5 = female pin header, 7 pins [form="♀ (female)"]
  J4 = female pin header, 7 pins [form="♀ (female)"]
  J3 = female pin header, 5 pins [form="♀ (female)"]
  J1 = female pin header, 6 pins [form="♀ (female)"]
  J2 = female pin header, 4 pins [form="♀ (female)"]
  J7 = female pin header, 2 pins [form="♀ (female)"]
  J10 = female pin header, 6 pins [form="♀ (female)"]
  J9 = female pin header, 6 pins [form="♀ (female)"]
  J8 = female pin header, 6 pins [form="♀ (female)"]
  J6 = female pin header, 2 pins [form="♀ (female)"]
  R2 = Resistor [tolerance=±5% resistance=10k package=THT]

nets:
  N1: ATMega328PU.RESET, R1.Pin_1
  N2: ATMega328PU.D0_(RX), J7.pin2
  N3: ATMega328PU.D1_(TX), J7.pin1
  N4: ATMega328PU.D2, J10.pin4
  N5: ATMega328PU.D3_(PWM), J10.pin5
  N6: ATMega328PU.D4, J10.pin6
  N7: ATMega328PU.VCC, ATMega328PU.AVCC, ATMega328PU.AREF, ATTiny85.Pin_8, R1.Pin_0, J2.pin1, J9.pin1, J9.pin2, J9.pin3, J9.pin4, J9.pin5, J9.pin6, R2.Pin_0
  N8: ATMega328PU.GND, ATTiny85.Pin_4, C1.0, C2.1, ULN_2003.0V, ULN_2003.COM_-_Common, J5.pin1, J5.pin2, J5.pin3, J5.pin4, J5.pin5, J5.pin6, J5.pin7, J2.pin2, J2.pin3, J2.pin4, J8.pin1, J8.pin2, J8.pin3, J8.pin4, J8.pin5, J8.pin6
  N9: ATMega328PU.XLAT1, XTAL1.pin_0, C2.0
  N10: ATMega328PU.XLAT2, XTAL1.pin_1, C1.1
  N11: ATMega328PU.D5_(PWM), J10.pin1
  N12: ATMega328PU.D6_(PWM), J10.pin2
  N13: ATMega328PU.D7, J10.pin3
  N14: ATMega328PU.D8, ATTiny85.Pin_5
  N15: ATMega328PU.D9_(PWM), ULN_2003.In_5, J3.pin5
  N16: ATMega328PU.D10_(PWM), ULN_2003.In_4, J3.pin4
  N17: ATMega328PU.D11_(PWM), ULN_2003.In_3, J3.pin3
  N18: ATMega328PU.D12, ULN_2003.In_1, J3.pin2
  N19: ATMega328PU.D13, ULN_2003.In_2, J3.pin1
  N20: ATMega328PU.A0, J1.pin6
  N21: ATMega328PU.A1, J1.pin5
  N22: ATMega328PU.A2, J1.pin4
  N23: ATMega328PU.A3, J1.pin3
  N24: ATMega328PU.A4, J1.pin2
  N25: ATMega328PU.A5, J1.pin1
  N26: ATTiny85.Pin_1, R2.Pin_1
  N27: ATTiny85.Pin_2, ULN_2003.In_7
  N28: ATTiny85.Pin_3, ULN_2003.In_6
  N29: ATTiny85.Pin_6, J6.pin1
  N30: ATTiny85.Pin_7, J6.pin2
  N31: ULN_2003.Out_7, J4.pin7
  N32: ULN_2003.Out_6, J4.pin6
  N33: ULN_2003.Out_5, J4.pin5
  N34: ULN_2003.Out_4, J4.pin4
  N35: ULN_2003.Out_3, J4.pin3
  N36: ULN_2003.Out_2, J4.pin2
  N37: ULN_2003.Out_1, J4.pin1

notes:
  right wheel pwm out
  left wheel pwm out
  right wheel speed encoder IN
  serial cmd in
  +5V Gnd Gnd +12V
  left wheel speed encoder IN
  right wheel 0v
  left wheel 0v
  right wheel +12v
  left wheel +12v
  digital out 0-4 0v
  digital out 0-4 +12v
  S/R
  S/L
  PWM3
  PWM4
  PWM5
  PWM0
  PWM1
  PWM2
  R
  L
  M0
  M1
  M2
  M3
  M4
  +12V
  GND
  +5V
  A0
  A1
  A2
  A3
  A4
  A5
  RX
  TX
  D0
  D1
  D2
  D3
  D4
  lnk
  XTAL1=16Mhz
  C1=C2=22pF
  R1=R2=10KOhm
  J1 digital/analog in
  J2 power supply
  J3 digital out
  J4 DC out 0v
  J5 DC out +12v
  J6 speed encoder in
  J7 host serial
  BAT-Controller v1.0
  BAT-C 1.0
  (c) B.A.T. Cave
