# Fritzing sketch SmartCarControllerHat-smt (saved by Fritzing 0.9.3b)
circuit board: 6.50052cm x 6.0891cm

parts:
  J4 = female pin header, 6 pins [form="♀ (female)"]
  J5 = female pin header, 6 pins [form="♀ (female)"]
  J6 = female pin header, 6 pins [form="♀ (female)"]  # not connected
  DC_12v = Power plug
  USB+ = female pin header, 1 pin [form="♀ (female)"]
  C5 = Electrolytic Capacitor [capacitance=470µF voltage=6.3V package="100 mil [THT, electrolytic]"]
  S4 = Pushbutton [package=THT]
  J9 = double row female pin header, 6 pins [form="♀ (female)"]
  RPi = Raspberry Pi 3 [part_number=RPI-3-V1.2]  # not connected
  USB- = female pin header, 1 pin [form="♀ (female)"]
  C4 = Ceramic Capacitor [capacitance=100nF package="100 mil [THT, multilayer]"]
  C3 = Ceramic Capacitor [capacitance=330nF package="100 mil [THT, multilayer]"]
  78L05 = Voltage Regulator - 5V [package="TO220 [THT]"]
  C6 = Electrolytic Capacitor [capacitance=470µF package="100 mil [THT, electrolytic]"]
  L1 = LED - 5mm [color="Red (633nm)" package="5 mm [THT]"]
  R3 = Resistor [tolerance=±5% resistance=470 package=THT]
  IC5 = SO14 [chip_label=ATTiny24/44/84 package=SO]
  R4 = Resistor [tolerance=±5% resistance=10k package=THT]
  U1 = atmega168 smd [package=tqfp]  # not connected

nets:
  N1: J4.pin1, J4.pin2, J4.pin3, J4.pin4, J4.pin5, J4.pin6, C5.-
  N2: J5.pin1, J5.pin2, J5.pin3, J5.pin4, J5.pin5, J5.pin6, C5.+
  GND: DC_12v.GND, USB-.pin1, C4.0, C3.0, 78L05.GND, C6.-
  N3: DC_12v.VCC, S4.leg1
  N4: USB+.pin1, S4.leg0, C3.1, 78L05.input_voltage, C6.+
  N5: J9.pin1, IC5.2
  N6: J9.pin2, J9.pin5, L1.cathode, IC5.14
  N7: J9.pin3, J9.pin4, IC5.1, R4.Pin_1
  N8: J9.pin6, IC5.3
  N9: C4.1, 78L05.output_voltage
  N10: L1.anode, R3.Pin_1
  N11: IC5.4, R4.Pin_0

notes:
  right wheel pwm out
  left wheel pwm out
  right wheel speed encoder IN
  serial cmd in
  +5V Gnd Gnd +12V
  left wheel speed encoder IN
  right wheel 0v
  left wheel 0v
  right wheel +12v
  left wheel +12v
  digital out 0-4 0v
  digital out 0-4 +12v
  link
  12v->USB
